# Fritzing sketch sensor-connections (saved by Fritzing 0.9.3b)
breadboards: 1

parts:
  R8 = Resistor [tolerance=±5% resistance=10k package=THT]
  R11 = Photocell (LDR) [part_number="LDR (CdSe)" package=THT]
  R12 = Temperature Sensor (Thermistor) [thermistor_type=NTC part_number=10k package=THT]
  R13 = Temperature Sensor (Thermistor) [thermistor_type=NTC part_number=10k package=THT]
  R14 = Resistor [tolerance=±5% resistance=10k package=THT]
  R15 = Resistor [tolerance=±5% resistance=10k package=THT]
  Part1 = Arduino Leonardo (Rev3b)
  Part2 = HC-SR501 Body Sensor Module [part_number="HC-SR501 PIR sensor"]

nets:
  5V: R8.Pin_0, R14.Pin_0, R15.Pin_0, Part1.5V, Part2.VCC
  N1: R8.Pin_1, R12.pin_0, Part1.A1
  N2: R11.pin_0, R14.Pin_1, Part1.A2
  GND: R11.pin_1, R12.pin_1, R13.pin_1, Part1.GND, Part2.GND
  N3: R13.pin_0, R15.Pin_1, Part1.A0
  N4: Part1.D9_PWM/A9, Part2.OUT

custom parts:
  HC-SR501 Body Sensor Module: Pyroelectric Infrared PIR Motion Sensor Detector Module
